// Logisim project TwentyOneBitDatapath.circ as structural Verilog: 6 circuits, main circuit Register_File
// Register
module Register_File (
  input  [20:0] in_1,
  input  in_2,
  input  [3:0] in_3,
  input  Clk,
  input  [3:0] in_5,
  input  [3:0] in_6,
  output [20:0] out_7,
  output [20:0] out_8
);

  wire decoder_1_out0, decoder_1_out1, decoder_1_out2, decoder_1_out3, decoder_1_out4, decoder_1_out5,
       decoder_1_out6, decoder_1_out7, decoder_1_out8, decoder_1_out9, decoder_1_out10, decoder_1_out11,
       decoder_1_out12, decoder_1_out13, decoder_1_out14, decoder_1_out15;
  wire [20:0] R0_q, R1_q, R2_q, R3_q, R4_q, R5_q, R6_q, R7_q, R8_q, R9_q, R10_q, R11_q, R12_q, R13_q, R14_q,
       R15_q;

  Decoder #(.select(4)) decoder_1 (
    .out0(decoder_1_out0), .out1(decoder_1_out1), .out2(decoder_1_out2), .out3(decoder_1_out3),
    .out4(decoder_1_out4), .out5(decoder_1_out5), .out6(decoder_1_out6), .out7(decoder_1_out7),
    .out8(decoder_1_out8), .out9(decoder_1_out9), .out10(decoder_1_out10), .out11(decoder_1_out11),
    .out12(decoder_1_out12), .out13(decoder_1_out13), .out14(decoder_1_out14), .out15(decoder_1_out15),
    .sel(in_3), .en(in_2));
  Register #(.width(21)) R0 (.D(in_1), .en(decoder_1_out0), .clk(Clk), .Q(R0_q));  // open: clr
  Register #(.width(21)) R1 (.D(in_1), .en(decoder_1_out1), .clk(Clk), .Q(R1_q));  // open: clr
  Register #(.width(21)) R2 (.D(in_1), .en(decoder_1_out2), .clk(Clk), .Q(R2_q), .clr(decoder_1_out6));
  Register #(.width(21)) R3 (.D(in_1), .en(decoder_1_out3), .clk(Clk), .Q(R3_q));  // open: clr
  Register #(.width(21)) R4 (.D(in_1), .en(decoder_1_out4), .clk(Clk), .Q(R4_q));  // open: clr
  Register #(.width(21)) R5 (.D(in_1), .en(decoder_1_out5), .clk(Clk), .Q(R5_q));  // open: clr
  Register #(.width(21)) R6 (.D(in_1), .en(decoder_1_out6), .clk(Clk), .Q(R6_q));  // open: clr
  Register #(.width(21)) R7 (.D(in_1), .en(decoder_1_out7), .clk(Clk), .Q(R7_q));  // open: clr
  Register #(.width(21)) R8 (.D(in_1), .en(decoder_1_out8), .clk(Clk), .Q(R8_q));  // open: clr
  Register #(.width(21)) R9 (.D(in_1), .en(decoder_1_out9), .clk(Clk), .Q(R9_q));  // open: clr
  Register #(.width(21)) R10 (.D(in_1), .en(decoder_1_out10), .clk(Clk), .Q(R10_q));  // open: clr
  Register #(.width(21)) R11 (.D(in_1), .en(decoder_1_out11), .clk(Clk), .Q(R11_q));  // open: clr
  Register #(.width(21)) R12 (.D(in_1), .en(decoder_1_out12), .clk(Clk), .Q(R12_q));  // open: clr
  Register #(.width(21)) R13 (.D(in_1), .en(decoder_1_out13), .clk(Clk), .Q(R13_q));  // open: clr
  Register #(.width(21)) R14 (.D(in_1), .en(decoder_1_out14), .clk(Clk), .Q(R14_q));  // open: clr
  Register #(.width(21)) R15 (.D(in_1), .en(decoder_1_out15), .clk(Clk), .Q(R15_q));  // open: clr
  Multiplexer #(.select(4), .width(21)) multiplexer_1 (
    .in0(R0_q), .in1(R1_q), .in2(R2_q), .in3(R3_q), .in4(R4_q), .in5(R5_q), .in6(R6_q), .in7(R7_q),
    .in8(R8_q), .in9(R9_q), .in10(R10_q), .in11(R11_q), .in12(R12_q), .in13(R13_q), .in14(R14_q),
    .in15(R15_q), .out(out_7), .sel(in_5));
  Multiplexer #(.select(4), .width(21)) multiplexer_2 (
    .in0(R0_q), .in1(R1_q), .in2(R2_q), .in3(R3_q), .in4(R4_q), .in5(R5_q), .in6(R6_q), .in7(R7_q),
    .in8(R8_q), .in9(R9_q), .in10(R10_q), .in11(R11_q), .in12(R12_q), .in13(R13_q), .in14(R14_q),
    .in15(R15_q), .out(out_8), .sel(in_6));

  // Notes on the sheet:
  //   Write_Enable
  //   Write_Address
  //   Read_Address_1
  //   Read_Address_2
  //   Write_Data
  //   Desiging of a Register File
  //   Output_Data_1
  //   Output_Data_2
endmodule

module Register_Test_File (
  input  [3:0] in_1,
  input  [3:0] in_2,
  input  [3:0] in_3,
  input  [20:0] in_4,
  input  in_5,
  output [20:0] out_6,
  output [20:0] out_7
);

  wire clock_1_out;

  Clock clock_1 (.out(clock_1_out));
  Register_File register_file_1 (
    .Clk(clock_1_out), .in_2(in_5), .in_3(in_3), .in_5(in_1), .in_6(in_2), .in_1(in_4), .out_8(out_7),
    .out_7(out_6));

  // Notes on the sheet:
  //   Register_Test_File
endmodule

module Datapath (
  input  in_1
);

  wire alu_21_bit_1_zero_signal, and_1_out, CLK_out, CLK_RAM_out, control_unit_1_alusrc,
       control_unit_1_branch, control_unit_1_jump, control_unit_1_memread, control_unit_1_memtoreg,
       control_unit_1_memwrite, control_unit_1_regdest, control_unit_1_regwrite;
  wire [3:0] multiplexer_3_out;
  wire [16:0] ROM_DATA_data;
  wire [20:0] adder_1_out, alu_21_bit_1_output_y, bit_extender_1_out, bit_extender_2_out, multiplexer_1_out,
       multiplexer_2_out, multiplexer_4_out, multiplexer_5_out, Program_Counter_q, RAM_DATA_dout,
       register_file_1_out_7, register_file_1_out_8;
  wire [20:17] control_unit_1_aluopcode;

  and and_1 (and_1_out, alu_21_bit_1_zero_signal, control_unit_1_branch);
  Multiplexer #(.width(21)) multiplexer_1 (
    .in0(adder_1_out), .in1(bit_extender_2_out), .out(multiplexer_1_out), .sel(and_1_out));
  Multiplexer #(.width(21)) multiplexer_2 (
    .in0(multiplexer_1_out), .in1(bit_extender_1_out), .out(multiplexer_2_out), .sel(control_unit_1_jump));
  Control_Unit control_unit_1 (
    .RegDest(control_unit_1_regdest), .RegWrite(control_unit_1_regwrite), .ALUSrc(control_unit_1_alusrc),
    .MemToReg(control_unit_1_memtoreg), .MemRead(control_unit_1_memread), .MemWrite(control_unit_1_memwrite),
    .Branch(control_unit_1_branch), .Jump(control_unit_1_jump), .ALUOpcode(control_unit_1_aluopcode));  // open: Opcode
  Register #(.width(21)) Program_Counter (
    .D(multiplexer_2_out), .en(in_1), .clk(CLK_out), .Q(Program_Counter_q));  // open: clr
  Adder #(.width(21)) adder_1 (.a(21'h1), .b(Program_Counter_q), .out(adder_1_out));  // open: cin, cout
  ROM #(.addrWidth(21), .dataWidth(21)) ROM_DATA (
    .addr(Program_Counter_q), .data({control_unit_1_aluopcode, ROM_DATA_data}));
  assign bit_extender_1_out = {{4{1'b0}}, ROM_DATA_data};  // Bit_Extender bit_extender_1
  Clock CLK (.out(CLK_out));
  Multiplexer #(.width(4)) multiplexer_3 (
    .in0(ROM_DATA_data[8:5]), .in1(ROM_DATA_data[12:9]), .out(multiplexer_3_out), .sel(control_unit_1_regdest));
  assign bit_extender_2_out = {{12{1'b0}}, ROM_DATA_data[8:0]};  // Bit_Extender bit_extender_2
  Register_File register_file_1 (
    .Clk(CLK_out), .in_2(control_unit_1_regwrite), .in_3(multiplexer_3_out), .in_5(ROM_DATA_data[16:13]),
    .in_6(ROM_DATA_data[12:9]), .in_1(multiplexer_5_out), .out_8(register_file_1_out_8),
    .out_7(register_file_1_out_7));
  Clock CLK_RAM (.out(CLK_RAM_out));
  Multiplexer #(.width(21)) multiplexer_4 (
    .in0(register_file_1_out_8), .in1(bit_extender_2_out), .out(multiplexer_4_out),
    .sel(control_unit_1_alusrc));
  ALU_21_Bit alu_21_bit_1 (
    .ALuoP(control_unit_1_aluopcode), .Shift_bit(ROM_DATA_data[4:0]), .B(multiplexer_4_out),
    .A(register_file_1_out_7), .Zero_Signal(alu_21_bit_1_zero_signal), .Output_Y(alu_21_bit_1_output_y));
  RAM #(.addrWidth(21), .dataWidth(21)) RAM_DATA (
    .addr(alu_21_bit_1_output_y), .we(control_unit_1_memwrite), .oe(control_unit_1_memread),
    .clk(CLK_RAM_out), .din(register_file_1_out_8), .dout(RAM_DATA_dout));
  Multiplexer #(.width(21)) multiplexer_5 (
    .in0(alu_21_bit_1_output_y), .in1(RAM_DATA_dout), .out(multiplexer_5_out), .sel(control_unit_1_memtoreg));

  // Notes on the sheet:
  //   Design of a  21-bit Processor Datapath
endmodule

// ALU
module ALU_21_Bit (
  input  [20:0] A,
  input  [20:0] B,
  input  [4:0] Shift_bit,
  input  [3:0] ALuoP,
  output [20:0] Output_Y,
  output Zero_Signal
);

  wire [20:0] adder_1_out, adder_2_out, shifter_1_out, shifter_2_out, subtractor_1_out, xor_1_out;

  Adder #(.width(21)) adder_1 (.a(A), .b(B), .out(adder_1_out));  // open: cin, cout
  Subtractor #(.width(21)) subtractor_1 (.a(A), .b(B), .out(subtractor_1_out));  // open: bin, bout
  Adder #(.width(21)) adder_2 (.a(A), .b(21'h1), .out(adder_2_out));  // open: cin, cout
  Shifter #(.width(21)) shifter_1 (.in(A), .\dist (Shift_bit), .out(shifter_1_out));
  Shifter #(.shift("lr"), .width(21)) shifter_2 (.in(A), .\dist (Shift_bit), .out(shifter_2_out));
  assign xor_1_out = A ^ B;  // XOR_Gate xor_1, 21 bits wide
  Multiplexer #(.select(4), .width(21)) multiplexer_1 (
    .in0(adder_1_out), .in1(subtractor_1_out), .in2(adder_2_out), .in3(shifter_1_out), .in4(shifter_2_out),
    .in5(xor_1_out), .out(Output_Y), .sel(ALuoP));  // open: in6, in7, in8, in9, in10, in11, in12, in13, in14, in15
  nor nor_1 (Zero_Signal, Output_Y[0], Output_Y[1], Output_Y[2], Output_Y[3], Output_Y[4], Output_Y[5], Output_Y[6], Output_Y[7], Output_Y[8], Output_Y[9], Output_Y[10], Output_Y[11], Output_Y[12], Output_Y[13], Output_Y[14], Output_Y[15], Output_Y[16], Output_Y[17], Output_Y[18], Output_Y[19], Output_Y[20]);

  // Notes on the sheet:
  //   Design a 21-bit ALU
  //   Operation Name |   OPcode
  //   ADD |   0000
  //   SUB |   0001
  //   INC |   0010
  //   SHL |   0011
  //   SHR |  0100
  //   XOR |   0101
endmodule

module ALU_Test_File (
  input  [3:0] in_1,
  input  [20:0] in_2,
  input  [4:0] in_3,
  input  [20:0] in_4,
  output [20:0] out_5
);

  ALU_21_Bit alu_21_bit_1 (.ALuoP(in_1), .Shift_bit(in_3), .B(in_4), .A(in_2), .Output_Y(out_5));  // open: Zero_Signal

  // Notes on the sheet:
  //   ALU_Test_File
  //   Operation Name |   OPcode
  //   ADD |   0000
  //   SUB |   0001
  //   INC |   0010
  //   SHL |   0011
  //   SHR |  0100
  //   XOR |   0101
endmodule

module Control_Unit (
  input  [3:0] Opcode,
  output [3:0] ALUOpcode,
  output RegDest,
  output RegWrite,
  output ALUSrc,
  output MemToReg,
  output MemRead,
  output MemWrite,
  output Branch,
  output Jump
);

  wire and_1_out, and_2_out, and_3_out, and_4_out, and_5_out, and_6_out, and_7_out, and_8_out, and_9_out,
       and_10_out, and_11_out, and_12_out, and_13_out, and_14_out, and_15_out, and_16_out, and_17_out,
       not_1_out, not_2_out, not_3_out, not_4_out;

  not not_1 (not_1_out, Opcode[3]);
  not not_2 (not_2_out, Opcode[2]);
  not not_3 (not_3_out, Opcode[1]);
  not not_4 (not_4_out, Opcode[0]);
  and and_1 (and_1_out, not_1_out, Opcode[2], not_3_out, Opcode[0]);
  and and_2 (and_2_out, Opcode[3], not_2_out, Opcode[0]);
  and and_3 (and_3_out, Opcode[3], Opcode[2], not_3_out, not_4_out);
  and and_4 (and_4_out, not_2_out, Opcode[1], Opcode[0]);
  and and_5 (and_5_out, not_1_out, Opcode[2], not_3_out, not_4_out);
  and and_6 (and_6_out, not_2_out, Opcode[1], not_4_out);
  and and_7 (and_7_out, Opcode[2], not_3_out, not_4_out);
  and and_8 (and_8_out, not_2_out, not_3_out, Opcode[0]);
  and and_9 (and_9_out, Opcode[2], Opcode[1]);
  and and_10 (and_10_out, Opcode[3], not_4_out);
  and and_11 (and_11_out, not_1_out, not_3_out);
  and and_12 (and_12_out, not_2_out, Opcode[1]);
  and and_13 (and_13_out, Opcode[2], not_4_out);
  and and_14 (and_14_out, not_2_out, not_3_out, Opcode[0]);
  and and_15 (and_15_out, Opcode[2], Opcode[1]);
  and and_16 (and_16_out, Opcode[3], Opcode[1], not_4_out);
  and and_17 (and_17_out, Opcode[3], Opcode[2]);
  and and_18 (MemToReg, Opcode[2], Opcode[1]);
  and and_19 (MemRead, Opcode[2], Opcode[1], not_4_out);
  and and_20 (MemWrite, Opcode[2], Opcode[1], Opcode[0]);
  and and_21 (Branch, Opcode[3], not_2_out, not_3_out, not_4_out);
  and and_22 (Jump, Opcode[3], not_3_out, Opcode[0]);
  or or_1 (ALUOpcode[2], and_1_out, and_2_out, and_3_out);
  or or_2 (ALUOpcode[1], and_4_out, and_5_out);
  or or_3 (ALUOpcode[0], and_6_out, and_7_out, Opcode[3]);
  or or_4 (RegDest, and_8_out, and_9_out, and_10_out);
  or or_5 (RegWrite, and_11_out, and_12_out, and_13_out);
  or or_6 (ALUSrc, and_14_out, and_15_out, and_16_out, and_17_out);

  assign ALUOpcode[3] = 1'b0;
endmodule
